// Logisim project olaf2.circ as structural Verilog: 6 circuits, main circuit main
module main (
  input  RST
);

  wire CLK_out, cpu_1_get, cpu_1_out, cpu_1_rst_out, RST_out;
  wire [6:0] keyboard_1_data;
  wire [7:0] bit_extender_1_out, cpu_1_ip, cpu_1_prnt_data, cpu_1_sp;
  wire [15:0] rom_1_data;

  Pull_Resistor pull_resistor_1 (.node(RST));
  Clock CLK (.out(CLK_out));
  or u_RST (RST_out, cpu_1_rst_out, RST);
  CPU cpu_1 (
    .CLK(CLK_out), .RST_IN(RST), .OPCODE(rom_1_data), .IP(cpu_1_ip), .RST_OUT(cpu_1_rst_out),
    .PRNT_DATA(cpu_1_prnt_data), .IN(bit_extender_1_out), .OUT(cpu_1_out), .GET(cpu_1_get), .SP(cpu_1_sp));
  ROM #(.dataWidth(16)) rom_1 (.addr(cpu_1_ip), .data(rom_1_data), .sel(1'b1));
  RAM ram_1 (.addr(cpu_1_sp), .sel(1'b1), .clk(CLK_out), .clr(RST_out));  // open: data, ld
  TTY tty_1 (.data(cpu_1_prnt_data[6:0]), .clk(CLK_out), .we(cpu_1_out), .clr(RST_out));
  Keyboard keyboard_1 (.clk(CLK_out), .re(cpu_1_get), .clr(RST_out), .data(keyboard_1_data));  // open: avail
  assign bit_extender_1_out = {{1{1'b0}}, keyboard_1_data};  // Bit_Extender bit_extender_1

  // Notes on the sheet:
  //   to fix:
  //   input
  //   ram
  //   read register
  //   not using 8-bit
  //   movr
  //   contents of rom_1 (hex, n*v repeats v):
  //   11b 20c 516 591a 612 4e1a a1a 341a 2b1a 351a 3d1a 347b 561 1a a1a 351a 2d1a 341a 3d1a 357b 462 1a
  //   a1a 351a 2a1a 341a 3d1a 47b 263 3061 1a a1a 381a 2f1a 341a 3d1a 87b 464 3061 1a a1a 391a 251a 341a
  //   3d1a 97b 465 3061 1a a1a 311a 3e1a 3e1a 331a 3d1a 17b 366 3061 1a a1a 381a 3c1a 3c1a 331a 3d1a 87b
  //   367 3061 1a a1a 351a 5e1a 371a 3d1a 77b 568 3061 1a a1a 351a 261a 331a 3d1a 57b 36a 3061 1a a1a 351a
  //   7c1a 321a 3d1a 57b 26b 3061 1a a1a c 8*0 1f
endmodule

module ALU (
  input  [7:0] SOURCE,
  input  [7:0] DEST,
  input  ADD,
  input  SUB,
  input  MUL,
  input  DIV,
  input  SHL,
  input  SHR,
  input  NOT,
  input  AND,
  input  OR,
  input  XOR,
  output CARRY,
  output BORROW,
  output ZERO,
  output [7:0] OUT,
  output [7:0] MOD,
  output ALU_USED
);

  wire not_2_out, not_3_out, not_4_out, not_5_out, not_6_out, not_7_out, not_8_out, not_9_out;
  wire [2:0] controlled_buffer_10_out, pull_resistor_6_node;
  wire [7:0] adder_1_out, and_1_out, controlled_buffer_1_out, controlled_buffer_2_out,
       controlled_buffer_3_out, controlled_buffer_4_out, controlled_buffer_5_out, controlled_buffer_6_out,
       controlled_buffer_7_out, controlled_buffer_8_out, controlled_buffer_13_out, controlled_buffer_14_out,
       controlled_buffer_15_out, controlled_buffer_16_out, controlled_buffer_17_out,
       controlled_buffer_18_out, divider_1_out, multiplier_1_out, not_1_out, or_2_out, pull_resistor_3_node,
       pull_resistor_5_node, pull_resistor_13_node, shifter_1_out, shifter_2_out, subtractor_1_out, xor_1_out;

  or or_1 (ALU_USED, ADD, SUB, MUL, DIV, SHL, SHR, NOT, AND, OR, XOR);
  assign controlled_buffer_1_out = ADD ? SOURCE : 8'bz;  // Controlled_Buffer controlled_buffer_1
  assign controlled_buffer_2_out = ADD ? DEST : 8'bz;  // Controlled_Buffer controlled_buffer_2
  assign controlled_buffer_3_out = SUB ? SOURCE : 8'bz;  // Controlled_Buffer controlled_buffer_3
  Pull_Resistor pull_resistor_1 (.node(controlled_buffer_3_out));
  assign controlled_buffer_4_out = SUB ? DEST : 8'bz;  // Controlled_Buffer controlled_buffer_4
  Pull_Resistor pull_resistor_2 (.node(controlled_buffer_4_out));
  assign controlled_buffer_5_out = MUL ? SOURCE : 8'bz;  // Controlled_Buffer controlled_buffer_5
  assign controlled_buffer_6_out = MUL ? DEST : 8'bz;  // Controlled_Buffer controlled_buffer_6
  assign controlled_buffer_7_out = DIV ? SOURCE : 8'bz;  // Controlled_Buffer controlled_buffer_7
  assign controlled_buffer_8_out = DIV ? DEST : 8'bz;  // Controlled_Buffer controlled_buffer_8
  Pull_Resistor pull_resistor_3 (.node(pull_resistor_3_node));
  assign pull_resistor_3_node = SHL ? SOURCE : 8'bz;  // Controlled_Buffer controlled_buffer_9
  assign controlled_buffer_10_out = SHL ? DEST[2:0] : 3'bz;  // Controlled_Buffer controlled_buffer_10
  Pull_Resistor pull_resistor_4 (.node(controlled_buffer_10_out));
  Pull_Resistor pull_resistor_5 (.node(pull_resistor_5_node));
  assign pull_resistor_5_node = SHR ? SOURCE : 8'bz;  // Controlled_Buffer controlled_buffer_11
  Pull_Resistor pull_resistor_6 (.node(pull_resistor_6_node));
  assign pull_resistor_6_node = SHR ? DEST[2:0] : 3'bz;  // Controlled_Buffer controlled_buffer_12
  assign controlled_buffer_13_out = NOT ? SOURCE : 8'bz;  // Controlled_Buffer controlled_buffer_13
  Pull_Resistor #(.pull(1)) pull_resistor_7 (.node(controlled_buffer_13_out));
  assign controlled_buffer_14_out = AND ? SOURCE : 8'bz;  // Controlled_Buffer controlled_buffer_14
  Pull_Resistor pull_resistor_8 (.node(controlled_buffer_14_out));
  assign controlled_buffer_15_out = AND ? DEST : 8'bz;  // Controlled_Buffer controlled_buffer_15
  Pull_Resistor pull_resistor_9 (.node(controlled_buffer_15_out));
  assign controlled_buffer_16_out = OR ? SOURCE : 8'bz;  // Controlled_Buffer controlled_buffer_16
  Pull_Resistor pull_resistor_10 (.node(controlled_buffer_16_out));
  assign controlled_buffer_17_out = OR ? DEST : 8'bz;  // Controlled_Buffer controlled_buffer_17
  Pull_Resistor pull_resistor_11 (.node(controlled_buffer_17_out));
  assign controlled_buffer_18_out = XOR ? SOURCE : 8'bz;  // Controlled_Buffer controlled_buffer_18
  Pull_Resistor pull_resistor_12 (.node(controlled_buffer_18_out));
  Pull_Resistor pull_resistor_13 (.node(pull_resistor_13_node));
  assign pull_resistor_13_node = XOR ? DEST : 8'bz;  // Controlled_Buffer controlled_buffer_19
  Adder adder_1 (
    .a(controlled_buffer_1_out), .b(controlled_buffer_2_out), .out(adder_1_out), .cout(CARRY));  // open: cin
  Subtractor subtractor_1 (
    .a(controlled_buffer_3_out), .b(controlled_buffer_4_out), .out(subtractor_1_out), .bin(1'b0),
    .bout(BORROW));
  Multiplier multiplier_1 (
    .a(controlled_buffer_5_out), .b(controlled_buffer_6_out), .out(multiplier_1_out), .cin({8{1'b0}}));  // open: cout
  Divider divider_1 (
    .a(controlled_buffer_7_out), .b(controlled_buffer_8_out), .out(divider_1_out), .upper({8{1'b0}}),
    .rem(MOD));
  Shifter shifter_1 (.in(pull_resistor_3_node), .\dist (controlled_buffer_10_out), .out(shifter_1_out));
  Shifter #(.shift("lr")) shifter_2 (.in(pull_resistor_5_node), .\dist (pull_resistor_6_node), .out(shifter_2_out));
  assign not_1_out = ~controlled_buffer_13_out;  // NOT_Gate not_1, 8 bits wide
  assign and_1_out = controlled_buffer_14_out & controlled_buffer_15_out;  // AND_Gate and_1, 8 bits wide
  assign or_2_out = controlled_buffer_16_out | controlled_buffer_17_out;  // OR_Gate or_2, 8 bits wide
  assign xor_1_out = controlled_buffer_18_out ^ pull_resistor_13_node;  // XOR_Gate xor_1, 8 bits wide
  Pull_Resistor pull_resistor_14 (.node(adder_1_out));
  Pull_Resistor pull_resistor_15 (.node(multiplier_1_out));
  Pull_Resistor pull_resistor_16 (.node(divider_1_out));
  Pull_Resistor pull_resistor_17 (.node(shifter_1_out));
  Pull_Resistor pull_resistor_18 ();  // open: node
  Pull_Resistor pull_resistor_19 (.node(not_1_out));
  Pull_Resistor pull_resistor_20 (.node(and_1_out));
  Pull_Resistor pull_resistor_21 (.node(or_2_out));
  Pull_Resistor pull_resistor_22 (.node(xor_1_out));
  Pull_Resistor pull_resistor_23 (.node(CARRY));
  Pull_Resistor pull_resistor_24 (.node(BORROW));
  ExactlyOne xor_2[7:0] (
    .out(OUT), .in0(adder_1_out), .in1(subtractor_1_out), .in2(multiplier_1_out), .in3(divider_1_out),
    .in4(shifter_1_out), .in5(shifter_2_out), .in6(not_1_out), .in7(and_1_out), .in8(or_2_out),
    .in9(xor_1_out));
  Pull_Resistor pull_resistor_25 (.node(MOD));
  not not_2 (not_2_out, OUT[0]);
  not not_3 (not_3_out, OUT[1]);
  not not_4 (not_4_out, OUT[2]);
  not not_5 (not_5_out, OUT[3]);
  not not_6 (not_6_out, OUT[4]);
  not not_7 (not_7_out, OUT[5]);
  not not_8 (not_8_out, OUT[6]);
  not not_9 (not_9_out, OUT[7]);
  Pull_Resistor pull_resistor_26 (.node(OUT));
  and and_2 (ZERO, not_2_out, not_3_out, not_4_out, not_5_out, not_6_out, not_7_out, not_8_out, not_9_out);
endmodule

module CPU (
  input  [7:0] IN,
  input  CLK,
  input  RST_IN,
  input  [15:0] OPCODE,
  output GET,
  output [7:0] PRNT_DATA,
  output OUT,
  output RST_OUT,
  output [7:0] IP,
  output [7:0] SP
);

  wire alu_1_alu_used, alu_1_borrow, alu_1_carry, alu_1_zero, controlled_buffer_2_out, decoder_1_out1,
       decoder_1_out2, decoder_1_out3, decoder_1_out4, decoder_1_out5, decoder_1_out6, decoder_1_out7,
       decoder_1_out8, decoder_1_out9, decoder_1_out10, decoder_1_out11, decoder_1_out12, decoder_1_out18,
       decoder_1_out19, decoder_1_out20, decoder_1_out21, decoder_1_out22, decoder_1_out23, decoder_1_out24,
       decoder_1_out26, decoder_1_out27, decoder_1_out28, decoder_1_out29, decoder_1_out30, DIV_out,
       flags_1_jmp_out, HAS_VALLUE_out, i_o_1_prnt, MOV_2_out, MOV_out, not_1_out, not_2_out, not_3_out,
       or_1_out, RST_out_2, SUB_out;
  wire [2:0] flags_1_ip_reg, i_o_1_data_reg, REG_out;
  wire [7:0] alu_1_mod, alu_1_out, controlled_buffer_1_out, controlled_buffer_3_out, controlled_buffer_4_out,
       controlled_buffer_6_out, controlled_buffer_7_out, i_o_1__in, multiplexer_1_out, or_2_out,
       pull_resistor_4_node, regs_1_ra, regs_1_rb, regs_1_rc, regs_1_rd, VAL_out;

  Decoder #(.select(5), .enable("false")) decoder_1 (
    .out1(decoder_1_out1), .out2(decoder_1_out2), .out3(decoder_1_out3), .out4(decoder_1_out4),
    .out5(decoder_1_out5), .out6(decoder_1_out6), .out7(decoder_1_out7), .out8(decoder_1_out8),
    .out9(decoder_1_out9), .out10(decoder_1_out10), .out11(decoder_1_out11), .out12(decoder_1_out12),
    .out18(decoder_1_out18), .out19(decoder_1_out19), .out20(decoder_1_out20), .out21(decoder_1_out21),
    .out22(decoder_1_out22), .out23(decoder_1_out23), .out24(decoder_1_out24), .out25(GET),
    .out26(decoder_1_out26), .out27(decoder_1_out27), .out28(decoder_1_out28), .out29(decoder_1_out29),
    .out30(decoder_1_out30), .out31(RST_OUT), .sel(OPCODE[4:0]));  // open: out0, out13, out14, out15, out16, out17
  or RST (RST_out_2, RST_OUT, RST_IN);
  or SUB (SUB_out, decoder_1_out2, decoder_1_out12);
  assign REG_out = flags_1_ip_reg | i_o_1_data_reg | OPCODE[7:5];  // OR_Gate REG, 3 bits wide
  assign controlled_buffer_1_out = or_1_out ? OPCODE[15:8] : 8'bz;  // Controlled_Buffer controlled_buffer_1
  Pull_Resistor pull_resistor_1 (.node(controlled_buffer_1_out));
  or or_1 (or_1_out, decoder_1_out27, flags_1_jmp_out);
  or HAS_VALLUE (HAS_VALLUE_out, OPCODE[8], OPCODE[9], OPCODE[10], OPCODE[11], OPCODE[12], OPCODE[13], OPCODE[14], OPCODE[15], 1'b0);
  or MOV (MOV_out, decoder_1_out27, flags_1_jmp_out, MOV_2_out, GET);
  assign VAL_out = controlled_buffer_1_out | i_o_1__in | or_2_out;  // OR_Gate VAL, 8 bits wide
  or DIV (DIV_out, decoder_1_out4, decoder_1_out5);
  FLAGS flags_1 (
    .JMP(decoder_1_out18), .JEQ(decoder_1_out19), .JNE(decoder_1_out20), .JBT(decoder_1_out21),
    .JST(decoder_1_out22), .JBE(decoder_1_out23), .JLE(decoder_1_out24), .BORROW(alu_1_borrow),
    .ZERO(alu_1_zero), .IP_REG(flags_1_ip_reg), .JMP_OUT(flags_1_jmp_out), .TEST(decoder_1_out12), .CLK(CLK),
    .RST(RST_out_2), .CARRY(alu_1_carry));
  assign controlled_buffer_2_out = decoder_1_out26 ? HAS_VALLUE_out : 1'bz;  // Controlled_Buffer controlled_buffer_2
  I_O i_o_1 (.GET(GET), .OUT(decoder_1_out26), .IN(IN), ._IN(i_o_1__in), .PRNT(i_o_1_prnt), .DATA_REG(i_o_1_data_reg));
  REGS regs_1 (
    .CLK(CLK), .RST(RST_out_2), .REG(REG_out), .VAL(VAL_out), .MOV(MOV_out), .RA(regs_1_ra), .RB(regs_1_rb),
    .RC(regs_1_rc), .RD(regs_1_rd), .IP(IP), .SP(SP), .PUSH(decoder_1_out28), .POP(decoder_1_out29),
    .RET(decoder_1_out30));
  Pull_Resistor pull_resistor_2 (.node(controlled_buffer_2_out));
  assign controlled_buffer_3_out = not_1_out ? controlled_buffer_4_out : 8'bz;  // Controlled_Buffer controlled_buffer_3
  Pull_Resistor pull_resistor_3 (.node(controlled_buffer_3_out));
  assign controlled_buffer_4_out = i_o_1_prnt ? regs_1_rd : 8'bz;  // Controlled_Buffer controlled_buffer_4
  not not_1 (not_1_out, controlled_buffer_2_out);
  assign PRNT_DATA = controlled_buffer_3_out | pull_resistor_4_node;  // OR_Gate PRT, 8 bits wide
  Pull_Resistor pull_resistor_4 (.node(pull_resistor_4_node));
  assign pull_resistor_4_node = controlled_buffer_2_out ? OPCODE[15:8] : 8'bz;  // Controlled_Buffer controlled_buffer_5
  ALU alu_1 (
    .SOURCE(multiplexer_1_out), .DEST(OPCODE[15:8]), .ADD(decoder_1_out1), .SUB(SUB_out),
    .MUL(decoder_1_out3), .DIV(DIV_out), .SHL(decoder_1_out6), .SHR(decoder_1_out7), .NOT(decoder_1_out9),
    .AND(decoder_1_out10), .OR(decoder_1_out11), .XOR(decoder_1_out8), .CARRY(alu_1_carry),
    .BORROW(alu_1_borrow), .ZERO(alu_1_zero), .OUT(alu_1_out), .MOD(alu_1_mod), .ALU_USED(alu_1_alu_used));
  and MOV_2 (MOV_2_out, alu_1_alu_used, not_2_out);
  not not_2 (not_2_out, decoder_1_out12);
  Pull_Resistor pull_resistor_5 (.node(PRNT_DATA));
  Multiplexer #(.select(3), .width(8), .enable("false")) multiplexer_1 (
    .in0(regs_1_ra), .in1(regs_1_rb), .in2(regs_1_rc), .in3(regs_1_rd), .in4(IP), .in5(SP),
    .out(multiplexer_1_out), .sel(REG_out));  // open: in6, in7
  DotMatrix #(.matrixcols(4), .matrixrows(8)) dotmatrix_1 (
    .col0(multiplexer_1_out), .col1(OPCODE[15:8]), .col2(alu_1_out), .col3(alu_1_mod));
  assign controlled_buffer_6_out = decoder_1_out5 ? alu_1_mod : 8'bz;  // Controlled_Buffer controlled_buffer_6
  not not_3 (not_3_out, decoder_1_out5);
  assign controlled_buffer_7_out = not_3_out ? alu_1_out : 8'bz;  // Controlled_Buffer controlled_buffer_7
  Pull_Resistor pull_resistor_6 (.node(controlled_buffer_7_out));
  Pull_Resistor pull_resistor_7 (.node(controlled_buffer_6_out));
  assign or_2_out = controlled_buffer_6_out | controlled_buffer_7_out;  // OR_Gate or_2, 8 bits wide
  Pull_Resistor pull_resistor_8 (.node(or_2_out));
  or or_3 (OUT, PRNT_DATA[0], PRNT_DATA[1], PRNT_DATA[2], PRNT_DATA[3], PRNT_DATA[4], PRNT_DATA[5], PRNT_DATA[6]);

  // Notes on the sheet:
  //   IN: pull=down
  //   OPCODE: pull=down
  //   out with data
endmodule

module FLAGS (
  input  TEST,
  input  CLK,
  input  RST,
  input  JMP,
  input  JEQ,
  input  JNE,
  input  JBT,
  input  BORROW,
  input  JST,
  input  CARRY,
  input  JBE,
  input  ZERO,
  input  JLE,
  output [2:0] IP_REG,
  output JMP_OUT
);

  wire and_1_out, and_2_out, and_3_out, and_4_out, and_5_out, and_6_out, and_7_out, and_8_out, not_1_out,
       not_2_out, not_3_out, or_1_out, or_2_out, register_1_q, register_3_q;

  not not_1 (not_1_out, register_3_q);
  and and_1 (and_1_out, register_1_q, JBT);
  not not_2 (not_2_out, register_1_q);
  and and_2 (and_2_out, not_2_out, JST);
  not not_3 (not_3_out, register_1_q);
  and and_3 (and_3_out, not_3_out, JBE);
  and and_4 (and_4_out, register_1_q, JLE);
  and and_5 (and_5_out, register_1_q, JBE);
  and and_6 (and_6_out, register_1_q, JLE);
  and and_7 (and_7_out, JEQ, register_3_q);
  and and_8 (and_8_out, JNE, not_1_out);
  or or_1 (or_1_out, and_3_out, and_5_out);
  or or_2 (or_2_out, and_4_out, and_6_out);
  assign IP_REG = JMP_OUT ? 3'b100 : 3'bz;  // Controlled_Buffer controlled_buffer_1
  Pull_Resistor pull_resistor_1 (.node(IP_REG));
  or or_3 (JMP_OUT, JMP, and_7_out, and_8_out, and_1_out, and_2_out, or_1_out, or_2_out);
  Register #(.width(1)) register_1 (.D(BORROW), .en(TEST), .Q(register_1_q), .clk(CLK), .clr(RST));
  Register #(.width(1)) register_2 (.D(CARRY), .en(TEST), .clk(CLK), .clr(RST));  // open: Q
  Register #(.width(1)) register_3 (.D(ZERO), .en(TEST), .Q(register_3_q), .clk(CLK), .clr(RST));

  // Notes on the sheet:
  //   CARRY: pull=down
  //   JBT: pull=down
  //   JEQ: pull=down
  //   RST: pull=down
  //   JNE: pull=down
  //   TEST: pull=down
  //   BORROW: pull=down
  //   ZERO: pull=down
  //   JMP: pull=down
  //   JBE: pull=down
  //   CLK: pull=down
  //   JST: pull=down
  //   JLE: pull=down
endmodule

module REGS (
  input  CLK,
  input  RST,
  input  [2:0] REG,
  input  [7:0] VAL,
  input  MOV,
  input  PUSH,
  input  POP,
  input  RET,
  output [7:0] RA,
  output [7:0] RB,
  output [7:0] RC,
  output [7:0] RD,
  output [7:0] IP,
  output [7:0] SP
);

  wire decoder_1_out0, decoder_1_out1, decoder_1_out2, decoder_1_out3, decoder_1_out4, decoder_1_out5,
       nor_1_out, not_1_out, not_2_out;
  wire [2:0] or_1_out, pull_resistor_1_node, pull_resistor_2_node;
  wire [7:0] adder_1_out, controlled_buffer_3_out, controlled_buffer_5_out, or_2_out, pull_resistor_3_node,
       subtractor_1_out;

  Decoder #(.select(3), .disabled(0)) decoder_1 (
    .out0(decoder_1_out0), .out1(decoder_1_out1), .out2(decoder_1_out2), .out3(decoder_1_out3),
    .out4(decoder_1_out4), .out5(decoder_1_out5), .sel(or_1_out), .en(MOV));  // open: out6, out7
  Pull_Resistor pull_resistor_1 (.node(pull_resistor_1_node));
  assign pull_resistor_1_node = not_1_out ? REG : 3'bz;  // Controlled_Buffer controlled_buffer_1
  not not_1 (not_1_out, RET);
  Pull_Resistor pull_resistor_2 (.node(pull_resistor_2_node));
  assign pull_resistor_2_node = RET ? 3'b100 : 3'bz;  // Controlled_Buffer controlled_buffer_2
  assign or_1_out = pull_resistor_1_node | pull_resistor_2_node;  // OR_Gate or_1, 3 bits wide
  Register u_RA (.D(VAL), .en(decoder_1_out0), .Q(RA), .clk(CLK), .clr(RST));
  Register u_RB (.D(VAL), .en(decoder_1_out1), .Q(RB), .clk(CLK), .clr(RST));
  Register u_RC (.D(VAL), .en(decoder_1_out2), .Q(RC), .clk(CLK), .clr(RST));
  Register u_RD (.D(VAL), .en(decoder_1_out3), .Q(RD), .clk(CLK), .clr(RST));
  not not_2 (not_2_out, decoder_1_out4);
  Subtractor subtractor_1 (.a(SP), .b(8'h8), .out(subtractor_1_out), .bin(1'b0));  // open: bout
  Adder adder_1 (.a(SP), .b(8'h8), .out(adder_1_out), .cin(1'b0));  // open: cout
  assign controlled_buffer_3_out = nor_1_out ? VAL : 8'bz;  // Controlled_Buffer controlled_buffer_3
  nor nor_1 (nor_1_out, PUSH, POP);
  Counter #(.ongoal("stay")) u_IP (
    .load(decoder_1_out4), .D(VAL), .count(not_2_out), .Q(IP), .clk(CLK), .clr(RST));  // open: carry
  Pull_Resistor pull_resistor_3 (.node(pull_resistor_3_node));
  assign pull_resistor_3_node = PUSH ? subtractor_1_out : 8'bz;  // Controlled_Buffer controlled_buffer_4
  assign controlled_buffer_5_out = POP ? adder_1_out : 8'bz;  // Controlled_Buffer controlled_buffer_5
  assign or_2_out = controlled_buffer_3_out | pull_resistor_3_node | controlled_buffer_5_out;  // OR_Gate or_2, 8 bits wide
  Pull_Resistor pull_resistor_4 (.node(controlled_buffer_5_out));
  Register u_SP (.D(or_2_out), .en(decoder_1_out5), .Q(SP), .clk(CLK), .clr(RST));

  // Notes on the sheet:
  //   POP: pull=down
  //   RST: pull=down
  //   CLK: pull=down
  //   MOV: pull=down
  //   REG: pull=down
  //   RET: pull=down
  //   PUSH: pull=down
endmodule

module I_O (
  input  [7:0] IN,
  input  GET,
  input  OUT,
  output [7:0] _IN,
  output PRNT,
  output [2:0] DATA_REG
);

  wire or_1_out;

  Pull_Resistor pull_resistor_1 (.node(_IN));
  assign _IN = GET ? IN : 8'bz;  // Controlled_Buffer controlled_buffer_1
  or or_1 (or_1_out, GET, OUT);
  Pull_Resistor pull_resistor_2 (.node(DATA_REG));
  assign DATA_REG = or_1_out ? 3'b011 : 3'bz;  // Controlled_Buffer controlled_buffer_2

  assign PRNT = OUT;

  // Notes on the sheet:
  //   GET: pull=down
  //   IN: pull=down
  //   OUT: pull=down
endmodule
